# Fritzing sketch Micropython-Home-Air-Quality-Station (saved by Fritzing 0.9.3b)
breadboards: 1

parts:
  M1 = DOIT Esp32 DevKit v1 (30 pins long, 11 pins width) [part_number=ESP32S-PIN30]
  DHT1 = DHT22 Humidity and Temperature Sensor
  USBUART1 = CP2102 USB UART Breakout
  part = Camdenboss CTB0158-6 [part_number=CTB0158-6 package=THT]
  R1 = Resistor [tolerance=±5% resistance=10k package=THT]

nets:
  3V3: M1.3V3, DHT1.VDD, R1.Pin_1
  GND: M1.GND, DHT1.GND, USBUART1.GND, part.pin2
  N1: M1.D4, DHT1.DATA, R1.Pin_0
  N2: M1.RX2, part.pin5
  N3: M1.TX2, part.pin4
  N4: M1.RX0, USBUART1.TXD
  N5: M1.VIN, part.pin1

notes:
  IDC PMS7003 Adapter
  [1] [2] [3] [4] [5] [6]
  1 - RST
  2 - TXD
  3 - RXD
  4 - SET
  5 - GND
  6 - VCC
  ESP32 DevKit V1
  DHT22
  10 kOhm resistor
  USB-UART Converter
  (optional)

custom parts:
  DOIT Esp32 DevKit v1 (30 pins long, 11 pins width): The DOIT Esp32 DevKit v1 is one of the development board created by DOIT to evaluate the ESP-WROOM-32 module. It is based on the ESP32 microcontroller that boasts Wifi, Bluetooth, Ethernet and Low Power support all in a single chip. (vanepp) made breadboard work, adjusted pin numbering and labels and reduced size of schematic and cleaned up pcb. This chip is 30pins long (2 x15) and 11 pins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
  CP2102 USB UART Breakout: CP2102 Usb Uart Breakout Board with Battery
